// Logisim project ALU-8bit_010422.circ as structural Verilog: 6 circuits, main circuit Half Adder
module ALU___8bit (
  input  in_1,
  input  in_2,
  input  [2:0] in_3,
  input  [7:0] A,
  input  [7:0] B,
  output [7:0] out_6,
  output out_7
);

  wire [7:0] rete_di_preelaborazione_1_a_out, rete_di_preelaborazione_1_b_out;

  rete_di_preelaborazione rete_di_preelaborazione_1 (
    .A_IN(A), .B_IN(B), .A_OUT(rete_di_preelaborazione_1_a_out), .B_OUT(rete_di_preelaborazione_1_b_out),
    .C2_C1_C0(in_3));
  Sommatore___8Bit_M sommatore_8bit_m_1 (
    .A(rete_di_preelaborazione_1_a_out), .B(rete_di_preelaborazione_1_b_out), .S(out_6), .CIn(in_1),
    .in_2(in_2), .COut(out_7));

  // Notes on the sheet:
  //   #CIRCUIT NAME: ALU - 8bit
endmodule

module rete_di_preelaborazione (
  input  [2:0] C2_C1_C0,
  input  [7:0] A_IN,
  input  [7:0] B_IN,
  output [7:0] A_OUT,
  output [7:0] B_OUT
);

  wire [7:0] multiplexer_1_out, not_1_out;

  Multiplexer #(.width(8), .enable("false")) multiplexer_1 (
    .in0(B_IN), .in1({8{1'b0}}), .out(multiplexer_1_out), .sel(C2_C1_C0[1]));
  assign not_1_out = ~multiplexer_1_out;  // NOT_Gate not_1, 8 bits wide
  Multiplexer #(.width(8), .enable("false")) multiplexer_2 (
    .in0(A_IN), .in1({8{1'b0}}), .out(A_OUT), .sel(C2_C1_C0[2]));
  Multiplexer #(.width(8), .enable("false")) multiplexer_3 (
    .in0(multiplexer_1_out), .in1(not_1_out), .out(B_OUT), .sel(C2_C1_C0[0]));

  // Notes on the sheet:
  //   #CIRCUIT NAME: Rete di Preelaborazione
endmodule

module Sommatore___8Bit_M (
  input  CIn,
  input  in_2,
  input  [7:0] A,
  input  [7:0] B,
  output [7:0] S,
  output COut
);

  wire and_1_out, and_2_out, and_3_out, and_4_out, and_5_out, and_6_out, and_7_out, full_adder_1_co,
       full_adder_2_co, full_adder_3_co, full_adder_4_co, full_adder_5_co, full_adder_6_co, full_adder_7_co;

  Full_Adder full_adder_1 (.CIn(CIn), .X(A[0]), .Y(B[0]), .S(S[0]), .CO(full_adder_1_co));
  Full_Adder full_adder_2 (.CIn(and_1_out), .X(A[1]), .Y(B[1]), .S(S[1]), .CO(full_adder_2_co));
  Full_Adder full_adder_3 (.CIn(and_2_out), .X(A[2]), .Y(B[2]), .S(S[2]), .CO(full_adder_3_co));
  Full_Adder full_adder_4 (.CIn(and_3_out), .X(A[3]), .Y(B[3]), .S(S[3]), .CO(full_adder_4_co));
  Full_Adder full_adder_5 (.CIn(and_4_out), .X(A[4]), .Y(B[4]), .S(S[4]), .CO(full_adder_5_co));
  Full_Adder full_adder_6 (.CIn(and_5_out), .X(A[5]), .Y(B[5]), .S(S[5]), .CO(full_adder_6_co));
  Full_Adder full_adder_7 (.CIn(and_6_out), .X(A[6]), .Y(B[6]), .S(S[6]), .CO(full_adder_7_co));
  Full_Adder full_adder_8 (.CIn(and_7_out), .X(A[7]), .Y(B[7]), .S(S[7]), .CO(COut));
  and and_1 (and_1_out, full_adder_1_co, in_2);
  and and_2 (and_2_out, full_adder_2_co, in_2);
  and and_3 (and_3_out, full_adder_3_co, in_2);
  and and_4 (and_4_out, full_adder_4_co, in_2);
  and and_5 (and_5_out, full_adder_5_co, in_2);
  and and_6 (and_6_out, full_adder_6_co, in_2);
  and and_7 (and_7_out, full_adder_7_co, in_2);

  // Notes on the sheet:
  //   #CIRCUIT NAME: Sommatore a 8Bit
  //   #NOTES: Aggiunto bit di modalità
endmodule

module Sommatore___8bit (
  input  CIn,
  input  [7:0] A,
  input  [7:0] B,
  output [7:0] S,
  output COut
);

  wire full_adder_1_co, full_adder_2_co, full_adder_3_co, full_adder_4_co, full_adder_5_co, full_adder_6_co,
       full_adder_7_co;

  Full_Adder full_adder_1 (.CIn(CIn), .X(A[0]), .Y(B[0]), .S(S[0]), .CO(full_adder_1_co));
  Full_Adder full_adder_2 (.CIn(full_adder_1_co), .X(A[1]), .Y(B[1]), .S(S[1]), .CO(full_adder_2_co));
  Full_Adder full_adder_3 (.CIn(full_adder_2_co), .X(A[2]), .Y(B[2]), .S(S[2]), .CO(full_adder_3_co));
  Full_Adder full_adder_4 (.CIn(full_adder_3_co), .X(A[3]), .Y(B[3]), .S(S[3]), .CO(full_adder_4_co));
  Full_Adder full_adder_5 (.CIn(full_adder_4_co), .X(A[4]), .Y(B[4]), .S(S[4]), .CO(full_adder_5_co));
  Full_Adder full_adder_6 (.CIn(full_adder_5_co), .X(A[5]), .Y(B[5]), .S(S[5]), .CO(full_adder_6_co));
  Full_Adder full_adder_7 (.CIn(full_adder_6_co), .X(A[6]), .Y(B[6]), .S(S[6]), .CO(full_adder_7_co));
  Full_Adder full_adder_8 (.CIn(full_adder_7_co), .X(A[7]), .Y(B[7]), .S(S[7]), .CO(COut));

  // Notes on the sheet:
  //   #CIRCUIT NAME: Sommatore a 8Bit
endmodule

module Full_Adder (
  input  CIn,
  input  X,
  input  Y,
  output S,
  output CO
);

  wire half_adder_1_co, half_adder_1_s, half_adder_2_co;

  Half_Adder half_adder_1 (.X(X), .Y(Y), .S(half_adder_1_s), .CO(half_adder_1_co));
  Half_Adder half_adder_2 (.X(CIn), .Y(half_adder_1_s), .S(S), .CO(half_adder_2_co));
  or or_1 (CO, half_adder_2_co, half_adder_1_co);

  // Notes on the sheet:
  //   #CIRCUIT NAME: Full Adder
endmodule

module Half_Adder (
  input  X,
  input  Y,
  output S,
  output CO
);

  xor xor_1 (S, X, Y);
  and and_1 (CO, X, Y);

  // Notes on the sheet:
  //   #CIRCUIT NAME: Half Adder
endmodule
