// Logisim project DATAPATH-8bit_010422.circ as structural Verilog: 1 circuit, main circuit main
module main (
  input  CK,
  input  M,
  input  [7:0] A,
  input  WE_A,
  input  WE_C,
  input  [7:0] B,
  input  WE_B,
  output [7:0] C,
  output Op_2
);

  wire [7:0] alu_8bit_1_out_6, multiplexer_1_out, multiplexer_2_out, multiplexer_3_out, register_1_q,
       register_2_q;

  Multiplexer #(.width(8), .enable("false")) multiplexer_1 (
    .in0(register_1_q), .in1(A), .out(multiplexer_1_out), .sel(WE_A));
  Register register_1 (.D(multiplexer_1_out), .en(1'b1), .Q(register_1_q), .clk(CK));  // open: clr
  Register register_2 (.D(multiplexer_2_out), .en(1'b1), .Q(register_2_q), .clk(CK));  // open: clr
  Multiplexer #(.width(8), .enable("false")) multiplexer_2 (
    .in0(register_2_q), .in1(B), .out(multiplexer_2_out), .sel(WE_B));
  // Probe on register_1_q
  // Probe on register_2_q
  ALU___8bit alu_8bit_1 (
    .A(register_1_q), .B(register_2_q), .out_6(alu_8bit_1_out_6), .in_3(3'b000), .in_1(1'b0), .in_2(M),
    .out_7(Op_2));
  // Probe on alu_8bit_1_out_6
  Multiplexer #(.width(8), .enable("false")) multiplexer_3 (
    .in0(C), .in1(alu_8bit_1_out_6), .out(multiplexer_3_out), .sel(WE_C));
  Register register_3 (.D(multiplexer_3_out), .en(1'b1), .Q(C), .clk(CK));  // open: clr

  // Notes on the sheet:
  //   #CIRCUIT NAME: Basic DATA PATH
  //   R1
  //   R2
  //   Op-1
  //   Risultato
  //   R3
endmodule
