// Logisim project miniCPU_010422.circ as structural Verilog: 1 circuit, main circuit main
module main (
  input  [7:0] A,
  input  [7:0] B,
  input  nReset,
  input  COD_OP,
  input  SF,
  output [7:0] C
);

  wire CK_out, main_1_u0, main_1_u1, main_1_u2;

  miniUDC_010422_main main_1 (
    .I0(SF), .I1(COD_OP), .I2(nReset), .U0(main_1_u0), .U1(main_1_u1), .U2(main_1_u2), .CK(CK_out));
  Clock CK (.out(CK_out));
  DATAPATH_8bit_010422_main main_2 (
    .A(A), .B(B), .C(C), .M(main_1_u2), .CK(CK_out), .WE_A(main_1_u1), .WE_B(main_1_u1), .WE_C(main_1_u0));  // open: Op_2
endmodule
