// Logisim project miniCPU_BUFFERS_010422.circ as structural Verilog: 1 circuit, main circuit main
module main (
  input  [7:0] A,
  input  [7:0] B,
  input  in_3,
  input  in_4,
  input  in_5,
  input  in_6
);

  wire CK;
  wire [7:0] main_1_c, register_1_q, register_2_q, register_3_q, register_4_q, register_5_q, register_6_q,
       register_7_q, register_8_q, register_9_q;

  DATAPATH_8bit_010422_main main_1 (
    .A(A), .B(B), .C(main_1_c), .M(in_3), .CK(CK), .WE_A(in_4), .WE_B(in_5), .WE_C(in_6));  // open: Op_2
  Clock clock_1 (.out(CK));
  // Probe on main_1_c
  Register register_1 (.D(A), .en(1'b1), .Q(register_1_q), .clk(CK));  // open: clr
  Register register_2 (.D(B), .en(1'b1), .Q(register_2_q), .clk(CK));  // open: clr
  Register register_3 (.D(main_1_c), .en(1'b1), .Q(register_3_q), .clk(CK));  // open: clr
  Register register_4 (.D(register_5_q), .en(1'b1), .Q(register_4_q), .clk(CK));  // open: clr
  Register register_5 (.D(register_1_q), .en(1'b1), .Q(register_5_q), .clk(CK));  // open: clr
  Register register_6 (.D(register_7_q), .en(1'b1), .Q(register_6_q), .clk(CK));  // open: clr
  Register register_7 (.D(register_2_q), .en(1'b1), .Q(register_7_q), .clk(CK));  // open: clr
  Register register_8 (.D(register_3_q), .en(1'b1), .Q(register_8_q), .clk(CK));  // open: clr
  Register register_9 (.D(register_8_q), .en(1'b1), .Q(register_9_q), .clk(CK));  // open: clr
  Register register_10 (.D(register_4_q), .en(1'b1), .clk(CK));  // open: Q, clr
  Register register_11 (.D(register_6_q), .en(1'b1), .clk(CK));  // open: Q, clr
  Register register_12 (.D(register_9_q), .en(1'b1), .clk(CK));  // open: Q, clr

  // Notes on the sheet:
  //   C
  //   # BUFFER B
  //   # BUFFER A
  //   # BUFFER C
endmodule
