// Logisim project miniUDC_010422.circ as structural Verilog: 1 circuit, main circuit main
module main (
  input  I0,
  input  I1,
  input  I2,
  input  CK,
  output U0,
  output U1,
  output U2
);

  wire and_1_out, and_2_out, and_3_out, and_4_out, and_5_out, d_ff_1_q, d_ff_3_q, not_1_out, not_2_out,
       not_3_out, not_4_out, not_5_out, not_6_out, not_7_out, or_1_out;

  not not_1 (not_1_out, U0);
  not not_2 (not_2_out, d_ff_1_q);
  not not_3 (not_3_out, I0);
  not not_4 (not_4_out, d_ff_3_q);
  not not_5 (not_5_out, U0);
  not not_6 (not_6_out, U0);
  not not_7 (not_7_out, U0);
  and and_1 (and_1_out, not_1_out, not_2_out, I2);
  and and_2 (and_2_out, U0, I2, I1, not_3_out);
  and and_3 (and_3_out, not_4_out, not_5_out, d_ff_1_q, I2, I1);
  and and_4 (and_4_out, not_6_out, d_ff_1_q, I2);
  and and_5 (and_5_out, U0, I2, I0);
  and and_6 (U1, not_7_out, d_ff_1_q, I2);
  and and_7 (U2, U0, d_ff_1_q);
  or or_1 (or_1_out, and_1_out, and_2_out, and_3_out);
  D_Flip_Flop d_ff_1 (.clk(CK), .D(or_1_out), .Q(d_ff_1_q));  // open: Qn, preset, en, reset
  D_Flip_Flop d_ff_2 (.clk(CK), .D(and_4_out), .Q(U0));  // open: Qn, preset, en, reset
  D_Flip_Flop d_ff_3 (.clk(CK), .D(and_5_out), .Q(d_ff_3_q));  // open: Qn, preset, en, reset

  // Notes on the sheet:
  //   q2
  //   q1
  //   q0
  //   CALCOLO USCITA
  //   CALCOLO STATO
  //   Q0
  //   Q1
  //   Q2
  //   q0
  //   q1
  //   q2
endmodule
