// Logisim project sommaSequenziale.circ as structural Verilog: 3 circuits, main circuit main
module main (
  input  in_1,
  input  in_2,
  output out_3,
  output out_4
);

  xor xor_1 (out_3, in_1, in_2);
  and and_1 (out_4, in_1, in_2);
endmodule

module fa (
  input  in_1,
  input  in_2,
  input  in_3,
  output out_4,
  output out_5
);

  wire main_1_out_3, main_1_out_4, main_2_out_4;

  main main_1 (.in_1(in_2), .in_2(in_3), .out_3(main_1_out_3), .out_4(main_1_out_4));
  main main_2 (.in_1(in_1), .in_2(main_1_out_3), .out_3(out_4), .out_4(main_2_out_4));
  or or_1 (out_5, main_2_out_4, main_1_out_4);
endmodule

module aluseq (
  input  CI,
  input  A0,
  input  A1,
  input  A2,
  input  Ai,
  input  A3,
  input  Bi,
  input  B0,
  input  B1,
  input  B2,
  input  B3,
  input  Ai_2,
  input  Bi_2,
  output S0,
  output S1,
  output Si,
  output S2,
  output S3,
  output CO,
  output Si_2
);

  wire CK, d_ff_1_q, d_ff_2_q, d_ff_3_q, d_ff_4_q, d_ff_5_q, d_ff_6_q, d_ff_7_q, d_ff_8_q, d_ff_9_q,
       d_ff_10_q, d_ff_11_q, d_ff_12_q, d_ff_13_q, fa_1_out_5, fa_2_out_5, fa_3_out_5, fa_5_out_4,
       fa_5_out_5, fa_6_out_5;

  D_Flip_Flop d_ff_1 (.clk(CK), .D(Ai_2), .Q(d_ff_1_q), .en(1'b1));  // open: Qn, preset, reset
  LED led_1 (.in(d_ff_1_q));
  D_Flip_Flop d_ff_2 (.clk(CK), .D(Bi_2), .Q(d_ff_2_q), .en(1'b1));  // open: Qn, preset, reset
  LED led_2 (.in(d_ff_2_q));
  D_Flip_Flop d_ff_3 (.clk(CK), .D(d_ff_1_q), .Q(d_ff_3_q), .en(1'b1));  // open: Qn, preset, reset
  LED led_3 (.in(d_ff_3_q));
  D_Flip_Flop d_ff_4 (.clk(CK), .D(d_ff_2_q), .Q(d_ff_4_q), .en(1'b1));  // open: Qn, preset, reset
  LED led_4 (.in(d_ff_4_q));
  fa fa_1 (.in_1(CI), .in_2(A0), .in_3(B0), .out_4(S0), .out_5(fa_1_out_5));
  fa fa_2 (.in_1(fa_1_out_5), .in_2(A1), .in_3(B1), .out_4(S1), .out_5(fa_2_out_5));
  fa fa_3 (.in_1(fa_2_out_5), .in_2(A2), .in_3(B2), .out_4(S2), .out_5(fa_3_out_5));
  fa fa_4 (.in_1(fa_3_out_5), .in_2(A3), .in_3(B3), .out_4(S3), .out_5(CO));
  D_Flip_Flop d_ff_5 (.clk(CK), .D(d_ff_3_q), .Q(d_ff_5_q), .en(1'b1));  // open: Qn, preset, reset
  LED led_5 (.in(d_ff_5_q));
  D_Flip_Flop d_ff_6 (.clk(CK), .D(d_ff_4_q), .Q(d_ff_6_q), .en(1'b1));  // open: Qn, preset, reset
  LED led_6 (.in(d_ff_6_q));
  D_Flip_Flop d_ff_7 (.clk(CK), .D(d_ff_5_q), .Q(d_ff_7_q), .en(1'b1));  // open: Qn, preset, reset
  LED led_7 (.in(d_ff_7_q));
  D_Flip_Flop d_ff_8 (.clk(CK), .D(d_ff_6_q), .Q(d_ff_8_q), .en(1'b1));  // open: Qn, preset, reset
  LED led_8 (.in(d_ff_8_q));
  fa fa_5 (.in_1(d_ff_9_q), .in_2(d_ff_7_q), .in_3(d_ff_8_q), .out_4(fa_5_out_4), .out_5(fa_5_out_5));
  Clock clock_1 (.out(CK));
  D_Flip_Flop d_ff_9 (.clk(CK), .D(fa_5_out_5), .Q(d_ff_9_q), .en(1'b1));  // open: Qn, preset, reset
  fa fa_6 (.in_1(d_ff_10_q), .in_2(Ai), .in_3(Bi), .out_4(Si), .out_5(fa_6_out_5));
  D_Flip_Flop d_ff_10 (.clk(CK), .D(fa_6_out_5), .Q(d_ff_10_q), .en(1'b1));  // open: Qn, preset, reset
  D_Flip_Flop d_ff_11 (.clk(CK), .D(d_ff_12_q), .Q(d_ff_11_q), .en(1'b1));  // open: Qn, preset, reset
  D_Flip_Flop d_ff_12 (.clk(CK), .D(fa_5_out_4), .Q(d_ff_12_q), .en(1'b1));  // open: Qn, preset, reset
  LED led_9 (.in(d_ff_12_q));
  D_Flip_Flop d_ff_13 (.clk(CK), .D(d_ff_11_q), .Q(d_ff_13_q), .en(1'b1));  // open: Qn, preset, reset
  LED led_10 (.in(d_ff_11_q));
  LED led_11 (.in(d_ff_13_q));
  D_Flip_Flop d_ff_14 (.clk(CK), .D(d_ff_13_q), .Q(Si_2), .en(1'b1));  // open: Qn, preset, reset
  LED led_12 (.in(Si_2));

  // Notes on the sheet:
  //   (BIT VERTICALI: PARALLELO)
  //   A3
  //   B3
  //   A2
  //   BIT ORIZZONTALI: SERIE
  //   B2
  //   #SOMMATORE COMBINATORIO
  //   A1
  //   B1
  //   A0
  //   B0
  //   #SOMMATORE SEQUENZIALE CON BUFFER
  //   #SOMMATORE SEQUENZIALE
  //   Cout (SF)
  //   Cin (stato presente)
  //   S3
  //   S2
  //   S1
  //   S0
endmodule
