// Logisim project LatchSR.circ as structural Verilog: 1 circuit, main circuit main
module main (
  input  S,
  input  R,
  output Q_neg,
  output Q
);

  nor nor_1 (Q_neg, S, Q);
  nor nor_2 (Q, Q_neg, R);
endmodule
