// Logisim project ROMCOUNTER.circ as structural Verilog: 2 circuits, main circuit main
module main (
  input  [4:0] in_1,
  input  [4:0] in_2,
  input  [15:0] IND1,
  input  [15:0] IND1_2,
  input  RESET_COUNTER,
  input  [4:0] in_6,
  input  [15:0] IND1_3,
  input  [4:0] in_8,
  input  [3:0] CPI,
  input  [5:0] COP,
  input  [4:0] in_11,
  input  [5:0] COP_2,
  output [19:0] out_13,
  output [19:0] out_14,
  output [31:0] out_15,
  output [31:0] out_16,
  output [19:0] out_17,
  output [19:0] out_18,
  output [31:0] out_19,
  output [31:0] out_20,
  output [19:0] out_21,
  output [31:0] out_22
);

  wire and_1_out, clock_1_out, clock_2_out, clock_3_out, clock_4_out, clock_5_out, counterconfront_1_out_3,
       xnor_1_out, xnor_2_out, xnor_3_out, xnor_4_out;
  wire [3:0] counter_1_q, counter_2_q, counter_3_q, counter_4_q, counter_5_q;
  wire [15:0] rom_1_data;
  wire [19:0] rom_7_data;
  wire [31:0] main_1_p6, main_2_p6, main_3_p6, main_4_p6, main_5_p6;

  Counter #(.width(4), .max('hf)) counter_1 (.Q(counter_1_q), .clk(clock_1_out));  // open: load, D, count, carry, clr
  Clock clock_1 (.out(clock_1_out));
  // SuperAlu_main main_1: pin names not known; wires that end beside it: {{16{1'b0}}, IND1_2}, {{28{1'b0}}, counter_1_q}, 2'b00, 1'b0, in_2, main_1_p6
  ROM #(.addrWidth(6), .dataWidth(16)) rom_1 (.addr(COP), .data(rom_1_data));  // open: sel
  Clock clock_2 (.out(clock_2_out));
  Counter #(.width(4), .max('hf)) counter_2 (.Q(counter_2_q), .clk(clock_2_out));  // open: load, D, count, carry, clr
  // SuperAlu_main main_2: pin names not known; wires that end beside it: {{16{1'b0}}, rom_1_data}, {{28{1'b0}}, counter_2_q}, 2'b00, 1'b0, in_8, main_2_p6
  ROM #(.addrWidth(16), .dataWidth(20)) rom_2 (.addr(main_1_p6[15:0]), .data(out_14));  // open: sel
  ROM #(.addrWidth(16), .dataWidth(32)) rom_3 (.addr(main_1_p6[15:0]), .data(out_16));  // open: sel
  ROM #(.addrWidth(16), .dataWidth(20)) rom_4 (.addr(main_2_p6[15:0]), .data(out_18));  // open: sel
  ROM #(.addrWidth(16), .dataWidth(32)) rom_5 (.addr(main_2_p6[15:0]), .data(out_20));  // open: sel
  ROM #(.dataWidth(32)) rom_6 ();  // open: addr, data, sel
  ROM #(.addrWidth(6), .dataWidth(20)) rom_7 (.addr(COP_2), .data(rom_7_data));  // open: sel
  Clock clock_3 (.out(clock_3_out));
  counterconfront counterconfront_1 (.in_1(rom_7_data[3:0]), .in_2(counter_3_q), .out_3(counterconfront_1_out_3));
  Clock clock_4 (.out(clock_4_out));
  Clock clock_5 (.out(clock_5_out));
  xnor xnor_1 (xnor_1_out, CPI[3], counter_5_q[3]);
  xnor xnor_2 (xnor_2_out, CPI[2], counter_5_q[2]);
  and and_1 (and_1_out, xnor_1_out, xnor_2_out, xnor_4_out, xnor_3_out);
  Counter #(.width(4), .max('hf)) counter_3 (
    .Q(counter_3_q), .clk(clock_3_out), .clr(counterconfront_1_out_3));  // open: load, D, count, carry
  Counter #(.width(4), .max('hf)) counter_4 (
    .Q(counter_4_q), .clk(clock_4_out), .clr(RESET_COUNTER));  // open: load, D, count, carry
  Counter #(.width(4), .max('hf)) counter_5 (
    .Q(counter_5_q), .clk(clock_5_out), .clr(and_1_out));  // open: load, D, count, carry
  xnor xnor_3 (xnor_3_out, CPI[0], counter_5_q[0]);
  xnor xnor_4 (xnor_4_out, CPI[1], counter_5_q[1]);
  // SuperAlu_main main_3: pin names not known; wires that end beside it: {{16{1'b0}}, IND1}, {{28{1'b0}}, counter_4_q}, 2'b00, 1'b0, in_1, main_3_p6
  // SuperAlu_main main_4: pin names not known; wires that end beside it: {{16{1'b0}}, IND1_3}, {{28{1'b0}}, counter_5_q}, 2'b00, 1'b0, in_6, main_4_p6
  // SuperAlu_main main_5: pin names not known; wires that end beside it: {{16{1'b0}}, rom_7_data[19:4]}, {{28{1'b0}}, counter_3_q}, 2'b00, 1'b0, in_11, main_5_p6
  ROM #(.addrWidth(16), .dataWidth(20)) rom_8 (.addr(main_3_p6[15:0]), .data(out_13));  // open: sel
  ROM #(.addrWidth(16), .dataWidth(32)) rom_9 (.addr(main_3_p6[15:0]), .data(out_15));  // open: sel
  ROM #(.addrWidth(16), .dataWidth(20)) rom_10 (.addr(main_4_p6[15:0]), .data(out_17));  // open: sel
  ROM #(.addrWidth(16), .dataWidth(32)) rom_11 (.addr(main_4_p6[15:0]), .data(out_19));  // open: sel
  ROM #(.addrWidth(16), .dataWidth(20)) rom_12 (.addr(main_5_p6[15:0]), .data(out_21));  // open: sel
  ROM #(.addrWidth(16), .dataWidth(32)) rom_13 (.addr(main_5_p6[15:0]), .data(out_22));  // open: sel

  // Notes on the sheet:
  //   #INDIRIZZO
  //   OFFSET
  //   (COUNTER 4Bit)
  //   NO COUNTER STOP
  //   PRIMA
  //   MICROISTRUZIONE
  //   #COP MEMORY
  //   #ALU MODALITA' SOMMA
  //   contents of rom_1 (hex, n*v repeats v):
  //   0 3
  //   (COUNTER 4Bit)
  //   IND1+OFFSET
  //   OFFSET
  //   PRIMA
  //   #INDIRIZZO
  //   MICROISTRUZIONE
  //   #ROM 2
  //   #ROM 1
  //   #ALU MODALITA' SOMMA
  //   contents of rom_2 (hex, n*v repeats v):
  //   0 0 80 0 0 80
  //   contents of rom_3 (hex, n*v repeats v):
  //   20404 80840 1000 20404 80849 1000
  //   IND1+OFFSET
  //   #Segnali di CTRL: 32-48
  //   #Segnali di CTRL: 0-31
  //   #ROM 2
  //   #ROM 1
  //   contents of rom_4 (hex, n*v repeats v):
  //   0 0 80
  //   contents of rom_5 (hex, n*v repeats v):
  //   20404 80840 1000 20404 80849 1000
  //   #Segnali di CTRL: 32-48
  //   #Segnali di CTRL: 0-31
  //   contents of rom_6 (hex, n*v repeats v):
  //   430800 4a62000
  //   COP MEMORY
  //   contents of rom_7 (hex, n*v repeats v):
  //   3 33
  //   #INDIRIZZO
  //   MICROISTRUZIONE
  //   (COUNTER 4Bit)
  //   PRIMA
  //   (COUNTER 4Bit)
  //   OFFSET
  //   (COUNTER 4Bit)
  //   CPI
  //   PRIMA
  //   #INDIRIZZO
  //   MICROISTRUZIONE
  //   OFFSET
  //   OFFSET
  //   WITH COP MEMORY
  //   PRIMA
  //   #INDIRIZZO
  //   MICROISTRUZIONE
  //   WITH MANUAL COUNTER STOP
  //   WITH XOR COUNTER STOP
  //   SEGNALE DI RESET COUNTER
  //   #ALU MODALITA' SOMMA
  //   #ALU MODALITA' SOMMA
  //   #ALU MODALITA' SOMMA
  //   IND1+OFFSET
  //   IND1+OFFSET
  //   SEGNALE DI RESET COUNTER
  //   IND1+OFFSET
  //   #ROM 2
  //   #ROM 1
  //   #ROM 2
  //   #ROM 1
  //   #ROM 2
  //   #ROM 1
  //   contents of rom_8 (hex, n*v repeats v):
  //   0 0 80 0 0 80
  //   contents of rom_9 (hex, n*v repeats v):
  //   20404 80840 1000 20404 80849 1000
  //   contents of rom_10 (hex, n*v repeats v):
  //   0 0 80 0 0 80
  //   contents of rom_11 (hex, n*v repeats v):
  //   20404 80840 1000 20404 80849 1000
  //   contents of rom_12 (hex, n*v repeats v):
  //   0 0 80 0 0 80
  //   contents of rom_13 (hex, n*v repeats v):
  //   20404 80840 1000 20404 80849 1000
  //   #Segnali di CTRL: 32-48
  //   #Segnali di CTRL: 0-31
  //   #Segnali di CTRL: 32-48
  //   #Segnali di CTRL: 0-31
  //   #Segnali di CTRL: 32-48
  //   #Segnali di CTRL: 0-31
endmodule

module counterconfront (
  input  [3:0] in_1,
  input  [3:0] in_2,
  output out_3
);

  wire xnor_1_out, xnor_2_out, xnor_3_out, xnor_4_out;

  xnor xnor_1 (xnor_1_out, in_1[3], in_2[3]);
  xnor xnor_2 (xnor_2_out, in_1[2], in_2[2]);
  xnor xnor_3 (xnor_3_out, in_1[0], in_2[0]);
  xnor xnor_4 (xnor_4_out, in_1[1], in_2[1]);
  and and_1 (out_3, xnor_1_out, xnor_2_out, xnor_4_out, xnor_3_out);
endmodule
