// Logisim project serieparall.circ as structural Verilog: 3 circuits, main circuit main
module main (
  input  [3:0] D,
  input  [3:0] D_2,
  input  CK,
  input  [3:0] D_3,
  input  WE,
  input  Ck_2,
  input  OE,
  input  CK_3,
  input  D_4,
  input  Ck_4,
  input  [3:0] D_5,
  input  OE_2,
  input  OE_3,
  input  CK_5,
  input  WE_2,
  input  WE_3,
  input  OE2,
  input  OE2_2,
  input  CI,
  input  [3:0] RS1,
  input  CK_6,
  input  [3:0] RS2,
  output [3:0] Q,
  output [3:0] Q_2,
  output [3:0] Q_3,
  output [3:0] Q_4,
  output [3:0] Q_5,
  output [3:0] Q_6,
  output [3:0] RD,
  output CO
);

  wire d_ff_1_q, d_ff_2_q, d_ff_3_q, d_ff_4_q, d_ff_5_q, d_ff_6_q, d_ff_7_q, d_ff_8_q, d_ff_9_q, d_ff_10_q,
       d_ff_11_q, d_ff_12_q, fa_1_out_4, fa_1_out_5, fa_2_out_4, fa_2_out_5, fa_3_out_4, fa_3_out_5,
       fa_4_out_4, FF0_2_q, FF0_q;
  wire [3:0] BUFFER_2_out, multiplexer_1_out, multiplexer_2_out, multiplexer_3_out, register_1_q,
       register_2_q, register_3_q, register_4_q, register_5_q, register_6_q, register_7_q, register_9_q,
       register_10_q, register_12_q, undriven;

  Register #(.width(4)) register_1 (.D(D), .en(1'b1), .Q(register_1_q), .clk(Ck_2));  // open: clr
  D_Flip_Flop d_ff_1 (.clk(Ck_4), .D(D_4), .Q(d_ff_1_q), .en(1'b1));  // open: Qn, preset, reset
  LED Q0 (.in(d_ff_1_q));
  Register #(.width(4)) register_2 (.D(register_1_q), .en(1'b1), .Q(register_2_q), .clk(Ck_2));  // open: clr
  D_Flip_Flop d_ff_2 (.clk(Ck_4), .D(d_ff_1_q), .Q(d_ff_2_q), .en(1'b1));  // open: Qn, preset, reset
  D_Flip_Flop FF0 (.clk(CK_6), .D(RS1[0]), .Q(FF0_q), .en(1'b1));  // open: Qn, preset, reset
  D_Flip_Flop d_ff_3 (.clk(CK_6), .D(RS1[1]), .Q(d_ff_3_q), .en(1'b1));  // open: Qn, preset, reset
  D_Flip_Flop d_ff_4 (.clk(CK_6), .D(RS1[2]), .Q(d_ff_4_q), .en(1'b1));  // open: Qn, preset, reset
  D_Flip_Flop d_ff_5 (.clk(CK_6), .D(RS1[3]), .Q(d_ff_5_q), .en(1'b1));  // open: Qn, preset, reset
  D_Flip_Flop FF0_2 (.clk(CK_6), .D(RS2[0]), .Q(FF0_2_q), .en(1'b1));  // open: Qn, preset, reset
  D_Flip_Flop d_ff_6 (.clk(CK_6), .D(RS2[1]), .Q(d_ff_6_q), .en(1'b1));  // open: Qn, preset, reset
  D_Flip_Flop d_ff_7 (.clk(CK_6), .D(RS2[2]), .Q(d_ff_7_q), .en(1'b1));  // open: Qn, preset, reset
  D_Flip_Flop d_ff_8 (.clk(CK_6), .D(RS2[3]), .Q(d_ff_8_q), .en(1'b1));  // open: Qn, preset, reset
  Register #(.width(4)) register_3 (.D(register_2_q), .en(1'b1), .Q(register_3_q), .clk(Ck_2));  // open: clr
  Register #(.width(4)) register_4 (.D(register_3_q), .en(1'b1), .Q(register_4_q), .clk(Ck_2));  // open: clr
  LED Q1 (.in(d_ff_2_q));
  Register #(.width(4)) register_5 (.D(register_4_q), .en(1'b1), .Q(register_5_q), .clk(Ck_2));  // open: clr
  D_Flip_Flop d_ff_9 (.clk(Ck_4), .D(d_ff_2_q), .Q(d_ff_9_q), .en(1'b1));  // open: Qn, preset, reset
  LED Q1_2 (.in(d_ff_9_q));
  Register #(.width(4)) register_6 (.D(register_5_q), .en(1'b1), .Q(register_6_q), .clk(Ck_2));  // open: clr
  D_Flip_Flop d_ff_10 (.clk(Ck_4), .D(d_ff_9_q), .Q(d_ff_10_q), .en(1'b1));  // open: Qn, preset, reset
  LED Q1_3 (.in(d_ff_10_q));
  Register #(.width(4)) register_7 (.D(register_6_q), .en(1'b1), .Q(register_7_q), .clk(Ck_2));  // open: clr
  Register #(.width(4)) register_8 (.D(register_7_q), .en(1'b1), .Q(Q), .clk(Ck_2));  // open: clr
  D_Flip_Flop d_ff_11 (.clk(Ck_4), .D(d_ff_10_q), .Q(d_ff_11_q), .en(1'b1));  // open: Qn, preset, reset
  LED Q1_4 (.in(d_ff_11_q));
  fa fa_1 (.in_1(CI), .in_2(FF0_q), .in_3(FF0_2_q), .out_4(fa_1_out_4), .out_5(fa_1_out_5));
  fa fa_2 (.in_1(fa_1_out_5), .in_2(d_ff_3_q), .in_3(d_ff_6_q), .out_4(fa_2_out_4), .out_5(fa_2_out_5));
  fa fa_3 (.in_1(fa_2_out_5), .in_2(d_ff_4_q), .in_3(d_ff_7_q), .out_4(fa_3_out_4), .out_5(fa_3_out_5));
  fa fa_4 (.in_1(fa_3_out_5), .in_2(d_ff_5_q), .in_3(d_ff_8_q), .out_4(fa_4_out_4), .out_5(CO));
  D_Flip_Flop d_ff_12 (.clk(Ck_4), .D(d_ff_11_q), .Q(d_ff_12_q), .en(1'b1));  // open: Qn, preset, reset
  Register #(.width(4)) register_9 (.D(D_3), .en(1'b1), .Q(register_9_q), .clk(CK_3));  // open: clr
  LED Q1_5 (.in(d_ff_12_q));
  D_Flip_Flop FF0_3 (.clk(CK_6), .D(fa_1_out_4), .Q(RD[0]), .en(1'b1));  // open: Qn, preset, reset
  D_Flip_Flop d_ff_13 (.clk(CK_6), .D(fa_2_out_4), .Q(RD[1]), .en(1'b1));  // open: Qn, preset, reset
  D_Flip_Flop d_ff_14 (.clk(CK_6), .D(fa_3_out_4), .Q(RD[2]), .en(1'b1));  // open: Qn, preset, reset
  D_Flip_Flop d_ff_15 (.clk(CK_6), .D(fa_4_out_4), .Q(RD[3]), .en(1'b1));  // open: Qn, preset, reset
  assign Q_3 = OE ? register_9_q : 4'bz;  // Controlled_Buffer BUFFER
  Multiplexer #(.width(4)) multiplexer_1 (
    .in0(register_10_q), .in1(D_5), .out(multiplexer_1_out), .sel(WE_3));  // open: en
  Register #(.width(4)) register_10 (.D(multiplexer_1_out), .en(1'b1), .Q(register_10_q), .clk(CK_5));  // open: clr
  assign BUFFER_2_out = OE_3 ? register_10_q : 4'bz;  // Controlled_Buffer BUFFER_2
  assign Q_6 = OE2_2 ? register_10_q : 4'bz;  // Controlled_Buffer BUFFER_2
  Multiplexer #(.width(4)) multiplexer_2 (.in0(undriven), .in1(D_2), .out(multiplexer_2_out), .sel(WE));  // open: en
  Register #(.width(4)) register_11 (.D(multiplexer_2_out), .en(1'b1), .Q(Q_2), .clk(CK));  // open: clr
  Multiplexer #(.width(4)) multiplexer_3 (
    .in0(register_12_q), .in1(BUFFER_2_out), .out(multiplexer_3_out), .sel(WE_2));  // open: en
  Register #(.width(4)) register_12 (.D(multiplexer_3_out), .en(1'b1), .Q(register_12_q), .clk(CK_5));  // open: clr
  assign Q_4 = OE_2 ? register_12_q : 4'bz;  // Controlled_Buffer BUFFER_3
  assign Q_5 = OE2 ? register_12_q : 4'bz;  // Controlled_Buffer BUFFER_2_2

  // Notes on the sheet:
  //   EN
  //   #REGISTRI IN SERIE
  //   EN
  //   EN
  //   #Collegamento in Serie
  //   Q0
  //   #A
  //   #B
  //   Q1
  //   A0
  //   A1
  //   A2
  //   A3
  //   B0
  //   B1
  //   B2
  //   B3
  //   EN
  //   Q1
  //   Q1
  //   Q1
  //   4BIT ADDER
  //   Q1
  //   #C
  //   #REGISTRO SORGENTE
  //   Q
  //   #WRITE ENABLE
  //   #REGISTRO DESTINAZIONE
endmodule

module ha (
  input  in_1,
  input  in_2,
  output out_3,
  output out_4
);

  xor xor_1 (out_3, in_1, in_2);
  and and_1 (out_4, in_1, in_2);
endmodule

module fa (
  input  in_1,
  input  in_2,
  input  in_3,
  output out_4,
  output out_5
);

  wire ha_1_out_3, ha_1_out_4, ha_2_out_4;

  ha ha_1 (.in_1(in_2), .in_2(in_3), .out_3(ha_1_out_3), .out_4(ha_1_out_4));
  ha ha_2 (.in_1(in_1), .in_2(ha_1_out_3), .out_3(out_4), .out_4(ha_2_out_4));
  or or_1 (out_5, ha_2_out_4, ha_1_out_4);
endmodule
